// Logisim project t2v0.circ as structural Verilog: 2 circuits, main circuit main
module main (
);

  wire brzrOK, clk, ULAsrc;
  wire [3:0] ULAop;
  wire [7:0] A, B, imm8, multiplexer_1_out;

  Clock #(.highDuration(2), .lowDuration(2)) clock_1 (.out(clk));
  Register PC ();  // open: D, en, clk, Q, clr
  // dual_port_ram MemInstEDados: pin names not known
  Multiplexer #(.width(8)) multiplexer_1 (.in0(imm8), .in1(B), .out(multiplexer_1_out), .sel(ULAsrc));
  ULA ula_1 (.A(A), .B(multiplexer_1_out), .Seletor(ULAop), .brzr(brzrOK));  // open: R
endmodule

module ULA (
  input  [7:0] A,
  input  [7:0] B,
  input  [3:0] Seletor,
  output brzr,
  output [7:0] R
);

  wire [7:0] R0, R1, R2, R3, R4, R5, R6, R7, R8, R9;

  Multiplexer #(.select(4), .width(8)) multiplexer_1 (
    .in0(R0), .in1(R1), .in2(R2), .in3(R3), .in4(R4), .in5(R5), .in6(R6), .in7(R7), .in8(R8), .in9(R9),
    .in10({8{1'b0}}), .in11({8{1'b0}}), .in12({8{1'b0}}), .in13({8{1'b0}}), .in14({8{1'b0}}),
    .in15({8{1'b0}}), .out(R), .sel(Seletor));
  assign R0 = ~B;  // NOT_Gate not_1, 8 bits wide
  assign R1 = A & B;  // AND_Gate and_1, 8 bits wide
  assign R2 = A | B;  // OR_Gate or_1, 8 bits wide
  assign R3 = A ^ B;  // XOR_Gate xor_1, 8 bits wide
  Adder adder_1 (.a(A), .b(B), .out(R4));  // open: cin, cout
  Subtractor subtractor_1 (.a(A), .b(B), .out(R5));  // open: bin, bout
  Subtractor subtractor_2 (.a(A), .b(8'h1), .out(R6));  // open: bin, bout
  Multiplier multiplier_1 (.a(A), .b(B), .out(R7));  // open: cin, cout
  Shifter shifter_1 (.in(A), .\dist (B[2:0]), .out(R8));
  Shifter #(.shift("rr")) shifter_2 (.in(A), .\dist (B[2:0]), .out(R9));
  Comparator comparator_1 (.a(A), .b({8{1'b0}}), .eq(brzr));  // open: gt, lt
  // also tied to GND on the sheet: {B[3], B[4], B[5], B[6], B[7]}

  // Notes on the sheet:
  //   Soma
  //   Sub
  //   Dec
  //   Mult
  //   Slr
  //   Srr
endmodule
