// Logisim project t3.circ as structural Verilog: 10 circuits, main circuit main
module main (
);

  wire and_1_out, and_2_out, brcomp, brzi, brzr, clk, Enmov, EnUla1, EnUla2, ji, jr, load, mov, movhl,
       or_1_out, or_2_out, reset, store, wbrldmov;
  wire [1:0] in3imm2, in4imm2, multiplexer_3_out, multiplexer_5_out;
  wire [2:0] Ulaop1, Ulaop2;
  wire [3:0] imm4br, imm4mov;
  wire [7:0] A, A1, Abranch, adder_1_out, addr, B, B1, bancoreg_1_branchrb, Bbranch, dado1, dado2, dadomov,
       datamem, extsinal8bits_1_imm8, imm8br, in3imm8, in4imm8, multiplexer_2_out, multiplexer_4_out, PC,
       rom_1_p2, stinmov;
  wire [7:2] inst3ULA, inst4ULA;
  wire [7:4] inst1LDST, inst2BRANCH;

  // ROM #(.line("quad")) rom_1: pin names not known; wires that end beside it: PC, rom_1_p2, {inst1LDST, imm4mov}, {inst2BRANCH, imm4br}, {inst3ULA, in3imm2}, {inst4ULA, in4imm2}
  Button u_reset (.out(reset));
  Multiplexer #(.width(8)) multiplexer_1 (.in0(8'h4), .in1(imm8br), .out(rom_1_p2), .sel(or_1_out));
  or or_1 (or_1_out, and_1_out, ji);
  and and_1 (and_1_out, brzi, brcomp);
  Clock clock_1 (.out(clk));
  Adder adder_1 (.a(PC), .b(rom_1_p2), .out(adder_1_out));  // open: cin, cout
  and and_2 (and_2_out, brzr, brcomp);
  Multiplexer #(.width(8)) multiplexer_2 (.in0(adder_1_out), .in1(Bbranch), .out(multiplexer_2_out), .sel(or_2_out));
  or or_2 (or_2_out, and_2_out, jr);
  Register u_Pc (.D(multiplexer_2_out), .en(1'b1), .clk(clk), .Q(PC), .clr(reset));
  Multiplexer #(.width(2)) multiplexer_3 (.in0(imm4mov[3:2]), .in1(2'b00), .out(multiplexer_3_out), .sel(mov));
  Multiplexer #(.width(8)) multiplexer_4 (.in0(datamem), .in1(dadomov), .out(multiplexer_4_out), .sel(mov));
  Multiplexer #(.width(2)) multiplexer_5 (.in0(imm4mov[3:2]), .in1(2'b00), .out(multiplexer_5_out), .sel(mov));
  compbrz compbrz_1 (.A(Abranch), .brzr(brcomp));
  extSinal8bits extsinal8bits_1 (.imm4(imm4br), .imm8(extsinal8bits_1_imm8));
  extSinal2b8b extsinal2b8b_1 (.imm2(in3imm2), .imm8(in3imm8));
  extSinal2b8b extsinal2b8b_2 (.imm2(in4imm2), .imm8(in4imm8));
  lookupulaop lookupulaop_1 (.Opcode(inst3ULA[7:4]), .Ulaop(Ulaop1));
  lookupulaop lookupulaop_2 (.Opcode(inst4ULA[7:4]), .Ulaop(Ulaop2));
  BancoReg bancoreg_1 (
    .clk(clk), .reset(reset), .d1(dado1), .d2(dado2), .dmemmov(multiplexer_4_out), .SelW1(inst3ULA[3:2]),
    .SelW2(inst4ULA[3:2]), .wld(wbrldmov), .Selld(multiplexer_3_out), .SelA(inst3ULA[3:2]), .SelB(in3imm2),
    .SelA1(inst4ULA[3:2]), .SelB1(in4imm2), .Selstaddr(imm4mov[1:0]), .Selstinmv(multiplexer_5_out),
    .Selbranchrb(imm4br[1:0]), .Selbranchra(imm4br[3:2]), .EnMov(Enmov), .EnUla1(EnUla1), .EnUla2(EnUla2),
    .brzir0(brzi), .A(A), .B(B), .A1(A1), .B1(B1), .staddr(addr), .stinmv(stinmov),
    .branchrb(bancoreg_1_branchrb), .branchra(Abranch));
  movhighmovlow movhighmovlow_1 (.A(stinmov), .imm(imm4mov), .Seletor(movhl), .R(dadomov));
  slr slr_1 (.A(extsinal8bits_1_imm8), .B(8'h2), .R(imm8br));
  slr slr_2 (.A(bancoreg_1_branchrb), .B(8'h2), .R(Bbranch));
  ULA Ula1 (.A(A), .B(B), .imm(in3imm8), .Seletor(Ulaop1), .en(EnUla1), .R(dado1));
  ULA Ula2 (.A(A1), .B(B1), .imm(in4imm8), .Seletor(Ulaop2), .en(EnUla2), .R(dado2));
  RAM #(.asyncread("true"), .clearpin("true")) MemDados (
    .addr(addr), .we(store), .oe(load), .clk(clk), .din(stinmov), .dout(datamem), .clr(reset));
  ROM #(.addrWidth(4), .dataWidth(4)) MemControleBranch (.addr(inst2BRANCH), .data({brzr, brzi, jr, ji}));
  ROM #(.addrWidth(4), .dataWidth(6)) MemControleSLM (
    .addr(inst1LDST), .data({load, store, wbrldmov, mov, movhl, Enmov}));

  // Other names for the same wires on the sheet: inst1LDST[3:0] = imm4mov; rb1[1:0] = imm4mov[1:0];
  //   ra1[1:0] = imm4mov[3:2]; opcode1[3:0] = inst1LDST; inst2BRANCH[3:0] = imm4br; rb2[1:0] = imm4br[1:0];
  //   ra2[1:0] = imm4br[3:2]; opcode2[3:0] = inst2BRANCH; inst3ULA[1:0] = in3imm2; rb3[1:0] = in3imm2;
  //   ra3[1:0] = inst3ULA[3:2]; opcode3[3:0] = inst3ULA[7:4]; inst4ULA[1:0] = in4imm2; rb4[1:0] = in4imm2;
  //   ra4[1:0] = inst4ULA[3:2]; opcode4[3:0] = inst4ULA[7:4]

  // Notes on the sheet:
  //   brzi
  //   contents of rom_1 (hex, n*v repeats v):
  //   61 f0 f0 f0 79 f0 a5 f0 51 f0 f0 f0 62 f0 95 f0 75 5*f0 84 f0 60 f0 f0 f 7c f0 f0 f0 52 4*f0 13 f0
  //   f0 59 f0 f0 a3 f0 3e a7 f0 62 5*f0 88 f0 60 f0 f0 f0 7e 5*f0 8c f0 7b 4*f0 14 f0 f0 51 f0 ab af 5b
  //   f0 a3 a7 f0 3d f0 f0 51 f0 ab af 5b 5*f0 a7 f0 4b f0 90 a5 41 f0 f0 ad f0 f0 88 f0 7c 5*f0 84 f0 59
  //   5*f0 94 f0 70 f0 f0 f0 48 5*f0 ab f0 58 f0 f0 f0 71 f0 f0 f0 48 f0 f0 f0 70 f0 f0 f0 40 5*f0 c0 f0
  //   f0 2 f0 f0 f0 30 f0 f0
  //   mov
  //   ld st
  //   brzr e jr
  //   brzi e ji
  //   inc
  //   inc
  //   Quatro instrucoes formam uma instrucao longa
  //   MemInst
  //   As subinstrucoes sao direcionadas para cada unidade funcional
  //   brzr e jr
  //   Escrita: seleciona ra para st ou r0 para mov
  //   ld mov write
  //   Leitura: seleciona ra para st ou r0 para mov
  //   ula1
  //   ula2
  //   st mov read
  //   ula1
  //   ula2
  //   Identificar se r0 == 0 em brzi ou brzr 
  //   Estender sinal para o inc
  //   Operacao movhigh movlow
  //   Selecionar ulaop de acordo com o opcode para ula1 e ula2
  //    brzr jr
  //   Shiftar imm em 2
  //   ra3
  //   rb3
  //   ra4
  //   rb4
  //   rb1
  //   ou entrada mov
  //   Shiftar imm em 2
  //   ra1: entrada de dados
  //   contents of MemControleBranch (hex, n*v repeats v):
  //   8 4 2 1
  //   contents of MemControleSLM (hex, n*v repeats v):
  //   4*0 29 10 d f
  //   Memorias de Controle
  //   TESTE Reseta a memDados se apertar reset
endmodule

module BancoReg (
  input  clk,
  input  reset,
  input  [7:0] d1,
  input  [7:0] d2,
  input  [7:0] dmemmov,
  input  [1:0] SelW1,
  input  [1:0] SelW2,
  input  wld,
  input  [1:0] Selld,
  input  [1:0] SelA,
  input  [1:0] SelB,
  input  [1:0] SelA1,
  input  [1:0] SelB1,
  input  [1:0] Selstaddr,
  input  [1:0] Selstinmv,
  input  [1:0] Selbranchrb,
  input  [1:0] Selbranchra,
  input  EnMov,
  input  EnUla1,
  input  EnUla2,
  input  brzir0,
  output [7:0] A,
  output [7:0] B,
  output [7:0] A1,
  output [7:0] B1,
  output [7:0] staddr,
  output [7:0] stinmv,
  output [7:0] branchrb,
  output [7:0] branchra
);

  wire and_1_out, or_1_out, or_2_out, or_3_out, or_4_out, w0, w0ldmov, w1, w1ld, w02, w2, w2ld, w3, w3ld,
       w12, w22, w32;
  wire [7:0] l0, l1, l2, l3, multiplexer_8_out, multiplexer_10_out, multiplexer_11_out, multiplexer_12_out,
       multiplexer_13_out, multiplexer_14_out, multiplexer_15_out, multiplexer_16_out, multiplexer_17_out;

  Demultiplexer #(.select(2)) demultiplexer_1 (.out0(w0), .out1(w1), .out2(w2), .out3(w3), .in(EnUla1), .sel(SelW1));
  Demultiplexer #(.select(2)) demultiplexer_2 (
    .out0(w02), .out1(w12), .out2(w22), .out3(w32), .in(EnUla2), .sel(SelW2));
  and and_1 (and_1_out, wld, EnMov);
  Demultiplexer #(.select(2)) demultiplexer_3 (
    .out0(w0ldmov), .out1(w1ld), .out2(w2ld), .out3(w3ld), .in(and_1_out), .sel(Selld));
  Multiplexer #(.select(2), .width(8)) multiplexer_1 (.in0(l0), .in1(l1), .in2(l2), .in3(l3), .out(A), .sel(SelA));
  Multiplexer #(.select(2), .width(8)) multiplexer_2 (.in0(l0), .in1(l1), .in2(l2), .in3(l3), .out(B), .sel(SelB));
  Multiplexer #(.select(2), .width(8)) multiplexer_3 (.in0(l0), .in1(l1), .in2(l2), .in3(l3), .out(A1), .sel(SelA1));
  Multiplexer #(.select(2), .width(8)) multiplexer_4 (.in0(l0), .in1(l1), .in2(l2), .in3(l3), .out(B1), .sel(SelB1));
  Multiplexer #(.select(2), .width(8)) multiplexer_5 (
    .in0(l0), .in1(l1), .in2(l2), .in3(l3), .out(staddr), .sel(Selstaddr));
  Multiplexer #(.select(2), .width(8)) multiplexer_6 (
    .in0(l0), .in1(l1), .in2(l2), .in3(l3), .out(stinmv), .sel(Selstinmv));
  Multiplexer #(.select(2), .width(8)) multiplexer_7 (
    .in0(l0), .in1(l1), .in2(l2), .in3(l3), .out(branchrb), .sel(Selbranchrb));
  Multiplexer #(.select(2), .width(8)) multiplexer_8 (
    .in0(l0), .in1(l1), .in2(l2), .in3(l3), .out(multiplexer_8_out), .sel(Selbranchra));
  Multiplexer #(.width(8)) multiplexer_9 (.in0(multiplexer_8_out), .in1(l0), .out(branchra), .sel(brzir0));
  Multiplexer #(.width(8)) multiplexer_10 (.in0(d1), .in1(d2), .out(multiplexer_10_out), .sel(w02));
  Multiplexer #(.width(8)) multiplexer_11 (.in0(d1), .in1(d2), .out(multiplexer_11_out), .sel(w12));
  Multiplexer #(.width(8)) multiplexer_12 (
    .in0(multiplexer_10_out), .in1(dmemmov), .out(multiplexer_12_out), .sel(w0ldmov));
  or or_1 (or_1_out, w0, w02, w0ldmov);
  or or_2 (or_2_out, w1, w12, w1ld);
  Register r0 (.D(multiplexer_12_out), .en(or_1_out), .clk(clk), .Q(l0), .clr(reset));
  Multiplexer #(.width(8)) multiplexer_13 (
    .in0(multiplexer_11_out), .in1(dmemmov), .out(multiplexer_13_out), .sel(w1ld));
  Register r1 (.D(multiplexer_13_out), .en(or_2_out), .clk(clk), .Q(l1), .clr(reset));
  Multiplexer #(.width(8)) multiplexer_14 (.in0(d1), .in1(d2), .out(multiplexer_14_out), .sel(w22));
  Multiplexer #(.width(8)) multiplexer_15 (.in0(d1), .in1(d2), .out(multiplexer_15_out), .sel(w32));
  or or_3 (or_3_out, w3, w32, w3ld);
  Multiplexer #(.width(8)) multiplexer_16 (
    .in0(multiplexer_14_out), .in1(dmemmov), .out(multiplexer_16_out), .sel(w2ld));
  or or_4 (or_4_out, w2, w22, w2ld);
  Multiplexer #(.width(8)) multiplexer_17 (
    .in0(multiplexer_15_out), .in1(dmemmov), .out(multiplexer_17_out), .sel(w3ld));
  Register r3 (.D(multiplexer_17_out), .en(or_3_out), .clk(clk), .Q(l3), .clr(reset));
  Register r2 (.D(multiplexer_16_out), .en(or_4_out), .clk(clk), .Q(l2), .clr(reset));

  // Other names for the same wires on the sheet: data1[7:0] = d1; data2[7:0] = d2; datamemmov[7:0] = dmemmov

  // Notes on the sheet:
  //   Tratar nop Ula2
  //   Tratar nop no mov
  //   Tratar nop Ula1
  //   Escrita 1
  //   Escrita 2
  //   Escrita ld mov
  //   Leitura branch
  //   Leitura A
  //   Leitura B
  //   Leitura A1
  //   Leitura B1
  //   Leitura St mov
  //   Leitura St mov
  //   Leitura branch
endmodule

module extSinal8bits (
  input  [3:0] imm4,
  output [7:0] imm8
);


  assign imm8 = {{5{imm4[3]}}, imm4[2:0]};
endmodule

module ULA (
  input  [7:0] A,
  input  [7:0] B,
  input  [7:0] imm,
  input  [2:0] Seletor,
  output en,
  output [7:0] R
);

  wire comparator_1_eq;
  wire [0:0] R4;
  wire [7:0] R0, R1, R2, R3, R5, R6, R7, undriven;

  Multiplexer #(.select(3), .width(8)) multiplexer_1 (
    .in0(R0), .in1(R1), .in2(R2), .in3(R3), .in4({{7{1'b0}}, R4[0]}), .in5(R5), .in6(R6), .in7(R7), .out(R),
    .sel(Seletor));
  Adder adder_1 (.a(A), .b(B), .out(R1));  // open: cin, cout
  Subtractor subtractor_1 (.a(A), .b(B), .out(R2));  // open: bin, bout
  assign R3 = A | B;  // OR_Gate or_1, 8 bits wide
  nor nor_1 (R4[0], B[0], B[1], B[2], B[3], B[4], B[5], B[6], B[7]);
  Adder adder_2 (.a(A), .b(imm), .out(R7));  // open: cin, cout
  slr slr_1 (.A(A), .B(B), .R(R5));
  srr srr_1 (.A(undriven), .B(B), .R(R6));
  Comparator #(.width(3)) comparator_1 (.a(Seletor), .b(3'b000), .eq(comparator_1_eq));  // open: gt, lt
  not not_1 (en, comparator_1_eq);

  // Other names for the same wires on the sheet: Sel[2:0] = Seletor

  // Notes on the sheet:
  //   Add
  //   Sub
  //   Inc
  //   se R0 ativado, ula nao escreve
  //   R0 eh usado para nop e inst nao aritmetica, ou seja, 
endmodule

module slr (
  input  [7:0] A,
  input  [7:0] B,
  output [7:0] R
);

  wire multiplexer_1_out, multiplexer_2_out, multiplexer_3_out, multiplexer_4_out, multiplexer_5_out,
       multiplexer_6_out, multiplexer_7_out, multiplexer_8_out, multiplexer_9_out, multiplexer_10_out,
       multiplexer_11_out, multiplexer_12_out, multiplexer_13_out, multiplexer_14_out, multiplexer_15_out,
       multiplexer_16_out, multiplexer_17_out, multiplexer_18_out, multiplexer_19_out, multiplexer_20_out,
       multiplexer_21_out, multiplexer_22_out, multiplexer_23_out, multiplexer_24_out, or_1_out;

  Multiplexer multiplexer_1 (.in0(A[0]), .in1(1'b0), .out(multiplexer_1_out), .sel(B[0]));
  Multiplexer multiplexer_2 (.in0(A[1]), .in1(A[0]), .out(multiplexer_2_out), .sel(B[0]));
  Multiplexer multiplexer_3 (.in0(A[2]), .in1(A[1]), .out(multiplexer_3_out), .sel(B[0]));
  Multiplexer multiplexer_4 (.in0(A[3]), .in1(A[2]), .out(multiplexer_4_out), .sel(B[0]));
  Multiplexer multiplexer_5 (.in0(A[4]), .in1(A[3]), .out(multiplexer_5_out), .sel(B[0]));
  Multiplexer multiplexer_6 (.in0(A[5]), .in1(A[4]), .out(multiplexer_6_out), .sel(B[0]));
  Multiplexer multiplexer_7 (.in0(A[6]), .in1(A[5]), .out(multiplexer_7_out), .sel(B[0]));
  Multiplexer multiplexer_8 (.in0(A[7]), .in1(A[6]), .out(multiplexer_8_out), .sel(B[0]));
  Multiplexer multiplexer_9 (.in0(multiplexer_1_out), .in1(1'b0), .out(multiplexer_9_out), .sel(B[1]));
  Multiplexer multiplexer_10 (.in0(multiplexer_2_out), .in1(1'b0), .out(multiplexer_10_out), .sel(B[1]));
  Multiplexer multiplexer_11 (.in0(multiplexer_3_out), .in1(multiplexer_1_out), .out(multiplexer_11_out), .sel(B[1]));
  Multiplexer multiplexer_12 (.in0(multiplexer_4_out), .in1(multiplexer_2_out), .out(multiplexer_12_out), .sel(B[1]));
  Multiplexer multiplexer_13 (.in0(multiplexer_5_out), .in1(multiplexer_3_out), .out(multiplexer_13_out), .sel(B[1]));
  Multiplexer multiplexer_14 (.in0(multiplexer_6_out), .in1(multiplexer_4_out), .out(multiplexer_14_out), .sel(B[1]));
  Multiplexer multiplexer_15 (.in0(multiplexer_7_out), .in1(multiplexer_5_out), .out(multiplexer_15_out), .sel(B[1]));
  Multiplexer multiplexer_16 (.in0(multiplexer_8_out), .in1(multiplexer_6_out), .out(multiplexer_16_out), .sel(B[1]));
  Multiplexer multiplexer_17 (.in0(multiplexer_9_out), .in1(1'b0), .out(multiplexer_17_out), .sel(B[2]));
  Multiplexer multiplexer_18 (.in0(multiplexer_10_out), .in1(1'b0), .out(multiplexer_18_out), .sel(B[2]));
  Multiplexer multiplexer_19 (.in0(multiplexer_11_out), .in1(1'b0), .out(multiplexer_19_out), .sel(B[2]));
  Multiplexer multiplexer_20 (.in0(multiplexer_12_out), .in1(1'b0), .out(multiplexer_20_out), .sel(B[2]));
  Multiplexer multiplexer_21 (.in0(multiplexer_13_out), .in1(multiplexer_9_out), .out(multiplexer_21_out), .sel(B[2]));
  Multiplexer multiplexer_22 (.in0(multiplexer_14_out), .in1(multiplexer_10_out), .out(multiplexer_22_out), .sel(B[2]));
  Multiplexer multiplexer_23 (.in0(multiplexer_15_out), .in1(multiplexer_11_out), .out(multiplexer_23_out), .sel(B[2]));
  Multiplexer multiplexer_24 (.in0(multiplexer_16_out), .in1(multiplexer_12_out), .out(multiplexer_24_out), .sel(B[2]));
  Multiplexer multiplexer_25 (.in0(multiplexer_17_out), .in1(1'b0), .out(R[0]), .sel(or_1_out));
  Multiplexer multiplexer_26 (.in0(multiplexer_18_out), .in1(1'b0), .out(R[1]), .sel(or_1_out));
  Multiplexer multiplexer_27 (.in0(multiplexer_19_out), .in1(1'b0), .out(R[2]), .sel(or_1_out));
  Multiplexer multiplexer_28 (.in0(multiplexer_20_out), .in1(1'b0), .out(R[3]), .sel(or_1_out));
  Multiplexer multiplexer_29 (.in0(multiplexer_21_out), .in1(1'b0), .out(R[4]), .sel(or_1_out));
  Multiplexer multiplexer_30 (.in0(multiplexer_22_out), .in1(1'b0), .out(R[5]), .sel(or_1_out));
  Multiplexer multiplexer_31 (.in0(multiplexer_23_out), .in1(1'b0), .out(R[6]), .sel(or_1_out));
  Multiplexer multiplexer_32 (.in0(multiplexer_24_out), .in1(1'b0), .out(R[7]), .sel(or_1_out));
  or or_1 (or_1_out, B[7], B[6], B[5], B[4], B[3]);

  // Other names for the same wires on the sheet: s0 = R[0]; s1 = R[1]; s2 = R[2]; s3 = R[3]; s4 = R[4]; s5 = R[5];
  //   s6 = R[6]; s7 = R[7]
endmodule

module srr (
  input  [7:0] A,
  input  [7:0] B,
  output [7:0] R
);

  wire multiplexer_1_out, multiplexer_2_out, multiplexer_3_out, multiplexer_4_out, multiplexer_5_out,
       multiplexer_6_out, multiplexer_7_out, multiplexer_8_out, multiplexer_9_out, multiplexer_10_out,
       multiplexer_11_out, multiplexer_12_out, multiplexer_13_out, multiplexer_14_out, multiplexer_15_out,
       multiplexer_16_out, multiplexer_17_out, multiplexer_18_out, multiplexer_19_out, multiplexer_20_out,
       multiplexer_21_out, multiplexer_22_out, multiplexer_23_out, multiplexer_24_out, or_1_out;

  Multiplexer multiplexer_1 (.in0(A[0]), .in1(A[1]), .out(multiplexer_1_out), .sel(B[0]));
  Multiplexer multiplexer_2 (.in0(A[1]), .in1(A[2]), .out(multiplexer_2_out), .sel(B[0]));
  Multiplexer multiplexer_3 (.in0(A[2]), .in1(A[3]), .out(multiplexer_3_out), .sel(B[0]));
  Multiplexer multiplexer_4 (.in0(A[3]), .in1(A[4]), .out(multiplexer_4_out), .sel(B[0]));
  Multiplexer multiplexer_5 (.in0(A[4]), .in1(A[5]), .out(multiplexer_5_out), .sel(B[0]));
  Multiplexer multiplexer_6 (.in0(A[5]), .in1(A[6]), .out(multiplexer_6_out), .sel(B[0]));
  Multiplexer multiplexer_7 (.in0(A[6]), .in1(A[7]), .out(multiplexer_7_out), .sel(B[0]));
  Multiplexer multiplexer_8 (.in0(A[7]), .in1(1'b0), .out(multiplexer_8_out), .sel(B[0]));
  Multiplexer multiplexer_9 (.in0(multiplexer_1_out), .in1(multiplexer_3_out), .out(multiplexer_9_out), .sel(B[1]));
  Multiplexer multiplexer_10 (.in0(multiplexer_2_out), .in1(multiplexer_4_out), .out(multiplexer_10_out), .sel(B[1]));
  Multiplexer multiplexer_11 (.in0(multiplexer_3_out), .in1(multiplexer_5_out), .out(multiplexer_11_out), .sel(B[1]));
  Multiplexer multiplexer_12 (.in0(multiplexer_4_out), .in1(multiplexer_6_out), .out(multiplexer_12_out), .sel(B[1]));
  Multiplexer multiplexer_13 (.in0(multiplexer_5_out), .in1(multiplexer_7_out), .out(multiplexer_13_out), .sel(B[1]));
  Multiplexer multiplexer_14 (.in0(multiplexer_6_out), .in1(multiplexer_8_out), .out(multiplexer_14_out), .sel(B[1]));
  Multiplexer multiplexer_15 (.in0(multiplexer_7_out), .in1(1'b0), .out(multiplexer_15_out), .sel(B[1]));
  Multiplexer multiplexer_16 (.in0(multiplexer_8_out), .in1(1'b0), .out(multiplexer_16_out), .sel(B[1]));
  Multiplexer multiplexer_17 (.in0(multiplexer_9_out), .in1(multiplexer_13_out), .out(multiplexer_17_out), .sel(B[2]));
  Multiplexer multiplexer_18 (.in0(multiplexer_10_out), .in1(multiplexer_14_out), .out(multiplexer_18_out), .sel(B[2]));
  Multiplexer multiplexer_19 (.in0(multiplexer_11_out), .in1(multiplexer_15_out), .out(multiplexer_19_out), .sel(B[2]));
  Multiplexer multiplexer_20 (.in0(multiplexer_12_out), .in1(multiplexer_16_out), .out(multiplexer_20_out), .sel(B[2]));
  Multiplexer multiplexer_21 (.in0(multiplexer_13_out), .in1(1'b0), .out(multiplexer_21_out), .sel(B[2]));
  Multiplexer multiplexer_22 (.in0(multiplexer_14_out), .in1(1'b0), .out(multiplexer_22_out), .sel(B[2]));
  Multiplexer multiplexer_23 (.in0(multiplexer_15_out), .in1(1'b0), .out(multiplexer_23_out), .sel(B[2]));
  Multiplexer multiplexer_24 (.in0(multiplexer_16_out), .in1(1'b0), .out(multiplexer_24_out), .sel(B[2]));
  Multiplexer multiplexer_25 (.in0(multiplexer_17_out), .in1(1'b0), .out(R[0]), .sel(or_1_out));
  Multiplexer multiplexer_26 (.in0(multiplexer_18_out), .in1(1'b0), .out(R[1]), .sel(or_1_out));
  Multiplexer multiplexer_27 (.in0(multiplexer_19_out), .in1(1'b0), .out(R[2]), .sel(or_1_out));
  Multiplexer multiplexer_28 (.in0(multiplexer_20_out), .in1(1'b0), .out(R[3]), .sel(or_1_out));
  Multiplexer multiplexer_29 (.in0(multiplexer_21_out), .in1(1'b0), .out(R[4]), .sel(or_1_out));
  Multiplexer multiplexer_30 (.in0(multiplexer_22_out), .in1(1'b0), .out(R[5]), .sel(or_1_out));
  Multiplexer multiplexer_31 (.in0(multiplexer_23_out), .in1(1'b0), .out(R[6]), .sel(or_1_out));
  Multiplexer multiplexer_32 (.in0(multiplexer_24_out), .in1(1'b0), .out(R[7]), .sel(or_1_out));
  or or_1 (or_1_out, B[7], B[6], B[5], B[4], B[3]);

  // Other names for the same wires on the sheet: s0 = R[0]; s1 = R[1]; s2 = R[2]; s3 = R[3]; s4 = R[4]; s5 = R[5];
  //   s6 = R[6]; s7 = R[7]
endmodule

module movhighmovlow (
  input  [7:0] A,
  input  [3:0] imm,
  input  Seletor,
  output [7:0] R
);

  Multiplexer #(.width(8)) multiplexer_1 (.in0({imm, A[3:0]}), .in1({A[7:4], imm}), .out(R), .sel(Seletor));

  // Notes on the sheet:
  //   High
  //   Low
endmodule

module compbrz (
  input  [7:0] A,
  output brzr
);

  Comparator comparator_1 (.a(A), .b({8{1'b0}}), .eq(brzr));  // open: gt, lt
endmodule

module lookupulaop (
  input  [3:0] Opcode,
  output [2:0] Ulaop
);

  ROM #(.addrWidth(4), .dataWidth(3)) rom_1 (.addr(Opcode), .data(Ulaop));

  // Notes on the sheet:
  //   contents of rom_1 (hex, n*v repeats v):
  //   8*0 1 2 7 3 4 5 6
endmodule

module extSinal2b8b (
  input  [1:0] imm2,
  output [7:0] imm8
);


  assign imm8 = {{7{imm2[1]}}, imm2[0]};
endmodule
